# Fritzing sketch morse-keyer (saved by Fritzing 1.0.4)
breadboards: 1

parts:
  Pro_Micro1 = SparkFun Pro Micro
  Part1 = TRRS 3.5mm Jack Breakout  # not connected
  Part2 = TRRS 3.5mm Jack Breakout  # not connected
  Q1 = TRANSISTOR_NPN [package=to-92]
  R1 = Resistor [tolerance=±5% power=0.25W resistance=10k package=THT]
  J1 = Piezo Speaker
  R2 = Resistor [tolerance=±5% power=0.25W resistance=10k package=THT]
  R3 = Resistor [tolerance=±5% power=0.25W resistance=10k package=THT]
  S1 = Toggle Switch [package=THT]
  S2 = Toggle Switch [package=THT]
  R4 = TRIMPOT [maximum_resistance=10kΩ knob_status=50% power=0.5W package=3386u]

nets:
  N1: Pro_Micro1.GND, Q1.E, J1.pin1, R2.Pin_0, S1.COM, R4.CW
  N2: Pro_Micro1.3, R2.Pin_1
  N3: Pro_Micro1.5, R3.Pin_1
  N4: Pro_Micro1.9, S2.COM
  N5: Pro_Micro1.10, R1.Pin_1
  N6: Pro_Micro1.A0, S1.L2
  N7: Pro_Micro1.A1, S1.L1
  N8: Pro_Micro1.A2, R4.WIPER
  N9: Pro_Micro1.RAW, R4.CCW
  N10: Q1.B, R1.Pin_0
  N11: J1.pin2, S2.L2

notes:
  Morse key input
  piezo transducer or can use another TRS audio jack for external speaker connection
  Keyer output to radio
  potentiometer to adjust WPM for Iambic modes
  jumper or toggle switch.
  Close pins 1 & 2 for Iambic-A
  Close pins 2 & 3 for Iambic-B
  Leave pins open for Straight key
  jumper or toggle switch.
  Close pins 1 & 2 for sidetone
  Arduino pro micro clone w/ ATmega32u4.
  Code compiled using Arduino Leonardo.
  USB interface used for keyboard emulation as well as serial input.

custom parts:
  SparkFun Pro Micro: The Pro Micro is similar to the Pro Mini except with an ATmega32U4 on board. The USB transceiver inside the 32U4 allows us to add USB connectivity on-board and do away with bulky external USB interface. Based on: https://github.com/unorthodox-engineers/unorthodox-arduino/blob/master/Unorthodox/fritzing/parts/Pro%20Micro.fzpz
